# Fritzing sketch localization-system (saved by Fritzing 0.9.2b)
stripboards: 2

parts:
  J1 = female pin header, 2 pins [form="♀ (female)"]  # not connected
  J2 = female pin header, 2 pins [form="♀ (female)"]  # not connected
  J3 = female pin header, 2 pins [form="♀ (female)"]  # not connected
  J4 = female pin header, 2 pins [form="♀ (female)"]  # not connected
  J5 = female pin header, 2 pins [form="♀ (female)"]  # not connected
  J6 = female pin header, 2 pins [form="♀ (female)"]  # not connected
  J7 = female pin header, 2 pins [form="♀ (female)"]  # not connected
  J8 = female pin header, 2 pins [form="♀ (female)"]  # not connected
  J9 = female pin header, 2 pins [form="♀ (female)"]  # not connected
  J10 = female pin header, 2 pins [form="♀ (female)"]  # not connected
  J11 = female pin header, 2 pins [form="♀ (female)"]  # not connected
  J12 = female pin header, 2 pins [form="♀ (female)"]  # not connected
  J13 = female pin header, 2 pins [form="♀ (female)"]  # not connected
  J14 = female pin header, 2 pins [form="♀ (female)"]  # not connected
  J15 = female pin header, 2 pins [form="♀ (female)"]  # not connected
  J16 = female pin header, 2 pins [form="♀ (female)"]
  J17 = female pin header, 2 pins [form="♀ (female)"]  # not connected
  J18 = female pin header, 2 pins [form="♀ (female)"]  # not connected
  J19 = female pin header, 2 pins [form="♀ (female)"]
  J20 = female pin header, 2 pins [form="♀ (female)"]  # not connected
  J21 = female pin header, 2 pins [form="♀ (female)"]  # not connected
  J22 = female pin header, 2 pins [form="♀ (female)"]  # not connected
  J27 = female pin header, 2 pins [form="♀ (female)"]
  J28 = female pin header, 2 pins [form="♀ (female)"]
  J29 = female pin header, 2 pins [form="♀ (female)"]
  J30 = female pin header, 2 pins [form="♀ (female)"]
  Raspberry_Pi1 = Raspberry Pi 2
  J31 = female pin header, 2 pins [form="♀ (female)"]
  C1 = Electrolytic Capacitor [capacitance=0.1µF package="100 mil [THT, electrolytic]"]
  C2 = Electrolytic Capacitor [capacitance=0.1µF package="100 mil [THT, electrolytic]"]
  C3 = Electrolytic Capacitor [capacitance=0.1µF package="100 mil [THT, electrolytic]"]
  C4 = Electrolytic Capacitor [capacitance=0.1µF package="100 mil [THT, electrolytic]"]
  J32 = female pin header, 2 pins [form="♀ (female)"]  # not connected
  J33 = female pin header, 2 pins [form="♀ (female)"]  # not connected
  J34 = female pin header, 2 pins [form="♀ (female)"]  # not connected
  J35 = female pin header, 2 pins [form="♀ (female)"]  # not connected
  J36 = female pin header, 2 pins [form="♀ (female)"]  # not connected
  J37 = female pin header, 2 pins [form="♀ (female)"]  # not connected
  J38 = female pin header, 2 pins [form="♀ (female)"]  # not connected
  J39 = female pin header, 2 pins [form="♀ (female)"]  # not connected
  J40 = Piezo Speaker
  MIC1 = Microphone
  MIC2 = Microphone
  J41 = female pin header, 2 pins [form="♀ (female)"]  # not connected
  J42 = female pin header, 2 pins [form="♀ (female)"]  # not connected
  J43 = female pin header, 2 pins [form="♀ (female)"]
  J44 = female pin header, 2 pins [form="♀ (female)"]  # not connected
  J45 = female pin header, 2 pins [form="♀ (female)"]  # not connected
  J46 = female pin header, 2 pins [form="♀ (female)"]  # not connected
  J47 = female pin header, 2 pins [form="♀ (female)"]  # not connected
  J48 = female pin header, 2 pins [form="♀ (female)"]
  J49 = female pin header, 2 pins [form="♀ (female)"]
  J50 = female pin header, 2 pins [form="♀ (female)"]  # not connected
  J51 = female pin header, 2 pins [form="♀ (female)"]
  J52 = female pin header, 2 pins [form="♀ (female)"]  # not connected
  J53 = female pin header, 2 pins [form="♀ (female)"]
  J54 = female pin header, 2 pins [form="♀ (female)"]  # not connected
  C5 = Ceramic Capacitor [capacitance=10nF package="100 mil [THT, multilayer]"]
  J55 = female pin header, 2 pins [form="♀ (female)"]
  J56 = female pin header, 2 pins [form="♀ (female)"]
  J57 = female pin header, 2 pins [form="♀ (female)"]
  J58 = female pin header, 2 pins [form="♀ (female)"]
  R1 = Resistor [tolerance=±5% resistance=1k package=THT]
  R2 = Resistor [tolerance=±5% resistance=100k package=THT]
  J59 = female pin header, 2 pins [form="♀ (female)"]
  J60 = female pin header, 2 pins [form="♀ (female)"]
  J61 = female pin header, 2 pins [form="♀ (female)"]
  J62 = female pin header, 2 pins [form="♀ (female)"]
  C6 = Ceramic Capacitor [capacitance=10nF package="100 mil [THT, multilayer]"]
  R3 = Resistor [tolerance=±5% resistance=1k package=THT]
  R4 = Resistor [tolerance=±5% resistance=100k package=THT]
  R6 = Resistor [tolerance=±5% resistance=2.2k package=THT]
  C8 = Ceramic Capacitor [capacitance=1nF package="100 mil [THT, multilayer]"]
  R7 = Resistor [tolerance=±5% resistance=2.2k package=THT]
  C7 = Ceramic Capacitor [capacitance=1nF package="100 mil [THT, multilayer]"]
  R8 = Resistor [tolerance=±5% resistance=3.9k package=THT]
  C9 = Ceramic Capacitor [capacitance=10nF package="100 mil [THT, multilayer]"]
  R9 = Resistor [tolerance=±5% resistance=100k package=THT]
  R10 = Resistor [tolerance=±5% resistance=100k package=THT]
  R11 = Resistor [tolerance=±5% resistance=100k package=THT]
  C10 = Electrolytic Capacitor [capacitance=10µF package="100 mil [THT, electrolytic]"]
  R12 = Resistor [tolerance=±5% resistance=3.9k package=THT]
  C11 = Ceramic Capacitor [capacitance=10nF package="100 mil [THT, multilayer]"]
  R13 = Resistor [tolerance=±5% resistance=100k package=THT]
  R14 = Resistor [tolerance=±5% resistance=100k package=THT]
  R15 = Resistor [tolerance=±5% resistance=100k package=THT]
  C12 = Electrolytic Capacitor [capacitance=10µF package="100 mil [THT, electrolytic]"]
  J63 = female pin header, 2 pins [form="♀ (female)"]  # not connected
  J64 = female pin header, 2 pins [form="♀ (female)"]  # not connected
  J65 = female pin header, 2 pins [form="♀ (female)"]  # not connected
  J66 = female pin header, 2 pins [form="♀ (female)"]
  J67 = female pin header, 2 pins [form="♀ (female)"]
  J68 = female pin header, 2 pins [form="♀ (female)"]  # not connected
  J70 = female pin header, 2 pins [form="♀ (female)"]
  J72 = female pin header, 2 pins [form="♀ (female)"]  # not connected
  J73 = female pin header, 2 pins [form="♀ (female)"]  # not connected
  J74 = female pin header, 2 pins [form="♀ (female)"]  # not connected
  J76 = female pin header, 2 pins [form="♀ (female)"]
  J77 = female pin header, 2 pins [form="♀ (female)"]  # not connected
  J78 = female pin header, 2 pins [form="♀ (female)"]
  J80 = female pin header, 2 pins [form="♀ (female)"]  # not connected
  C13 = Electrolytic Capacitor [capacitance=0.1µF package="100 mil [THT, electrolytic]"]
  C14 = Electrolytic Capacitor [capacitance=0.1µF package="100 mil [THT, electrolytic]"]
  J81 = female pin header, 2 pins [form="♀ (female)"]  # not connected
  C15 = Electrolytic Capacitor [capacitance=0.1µF package="100 mil [THT, electrolytic]"]
  C16 = Electrolytic Capacitor [capacitance=0.1µF package="100 mil [THT, electrolytic]"]
  J82 = female pin header, 2 pins [form="♀ (female)"]
  J83 = female pin header, 2 pins [form="♀ (female)"]  # not connected
  J84 = female pin header, 2 pins [form="♀ (female)"]  # not connected
  J85 = female pin header, 2 pins [form="♀ (female)"]
  J86 = female pin header, 2 pins [form="♀ (female)"]  # not connected
  J87 = female pin header, 2 pins [form="♀ (female)"]  # not connected
  J88 = female pin header, 2 pins [form="♀ (female)"]  # not connected
  J89 = female pin header, 2 pins [form="♀ (female)"]  # not connected
  J90 = female pin header, 2 pins [form="♀ (female)"]
  J91 = female pin header, 2 pins [form="♀ (female)"]  # not connected
  J92 = female pin header, 2 pins [form="♀ (female)"]  # not connected
  J93 = female pin header, 2 pins [form="♀ (female)"]  # not connected
  J94 = female pin header, 2 pins [form="♀ (female)"]
  J95 = female pin header, 2 pins [form="♀ (female)"]  # not connected
  J96 = female pin header, 2 pins [form="♀ (female)"]  # not connected
  J97 = female pin header, 2 pins [form="♀ (female)"]
  J98 = female pin header, 2 pins [form="♀ (female)"]  # not connected
  J99 = female pin header, 2 pins [form="♀ (female)"]  # not connected
  J100 = female pin header, 2 pins [form="♀ (female)"]  # not connected
  J101 = female pin header, 2 pins [form="♀ (female)"]
  J102 = female pin header, 2 pins [form="♀ (female)"]
  J103 = female pin header, 2 pins [form="♀ (female)"]  # not connected
  J104 = Piezo Speaker
  J105 = female pin header, 2 pins [form="♀ (female)"]
  J106 = female pin header, 2 pins [form="♀ (female)"]
  J107 = female pin header, 2 pins [form="♀ (female)"]  # not connected
  MIC3 = Microphone
  C18 = Ceramic Capacitor [capacitance=10nF package="100 mil [THT, multilayer]"]
  J108 = female pin header, 2 pins [form="♀ (female)"]  # not connected
  J109 = female pin header, 2 pins [form="♀ (female)"]  # not connected
  R18 = Resistor [tolerance=±5% resistance=100k package=THT]
  J110 = female pin header, 2 pins [form="♀ (female)"]  # not connected
  J111 = female pin header, 2 pins [form="♀ (female)"]  # not connected
  J112 = female pin header, 2 pins [form="♀ (female)"]  # not connected
  J113 = female pin header, 2 pins [form="♀ (female)"]  # not connected
  J114 = female pin header, 2 pins [form="♀ (female)"]  # not connected
  J115 = female pin header, 2 pins [form="♀ (female)"]  # not connected
  J116 = female pin header, 2 pins [form="♀ (female)"]  # not connected
  J117 = female pin header, 2 pins [form="♀ (female)"]  # not connected
  J118 = female pin header, 2 pins [form="♀ (female)"]  # not connected
  J119 = female pin header, 2 pins [form="♀ (female)"]  # not connected
  J120 = female pin header, 2 pins [form="♀ (female)"]
  C19 = Ceramic Capacitor [capacitance=1nF package="100 mil [THT, multilayer]"]
  R19 = Resistor [tolerance=±5% resistance=1k package=THT]
  R20 = Resistor [tolerance=±5% resistance=2.2k package=THT]
  R23 = Resistor [tolerance=±5% resistance=3.9k package=THT]
  C22 = Ceramic Capacitor [capacitance=10nF package="100 mil [THT, multilayer]"]
  R25 = Resistor [tolerance=±5% resistance=100k package=THT]
  R27 = Resistor [tolerance=±5% resistance=100k package=THT]
  R28 = Resistor [tolerance=±5% resistance=100k package=THT]
  C24 = Electrolytic Capacitor [capacitance=10µF package="100 mil [THT, electrolytic]"]
  C25 = Ceramic Capacitor [capacitance=100nF package="100 mil [THT, multilayer]"]
  C26 = Ceramic Capacitor [capacitance=100nF package="100 mil [THT, multilayer]"]
  D1 = Rectifier Diode [part_number=1N4001 package="300 mil [THT]"]
  U1 = Voltage Regulator - 5V [package="TO220 [THT]"]
  VCC1 = Battery block 9V
  C27 = Electrolytic Capacitor [capacitance=1µF package="100 mil [THT, electrolytic]"]
  C28 = Electrolytic Capacitor [capacitance=10µF package="100 mil [THT, electrolytic]"]
  D2 = Rectifier Diode [part_number=1N4001 package="300 mil [THT]"]
  L1 = Inductor [inductance=300µH package="400 mil [THT]"]
  C29 = Ceramic Capacitor [capacitance=470nF package="100 mil [THT, multilayer]"]
  C30 = Electrolytic Capacitor [capacitance=1µF package="100 mil [THT, electrolytic]"]

nets:
  N1: J16.pin1, C4.-
  N2: J16.pin2, C2.-
  N3: J19.pin1, J43.pin1
  N4: J27.pin2, J40.pin2
  N5: J28.pin1, Raspberry_Pi1.GND, J31.pin2, C4.+, J40.pin1, MIC1.pin1, MIC2.pin1, J49.pin1, C5.1, J57.pin2, J61.pin2, C6.1, C8.0, R8.Pin_1, R11.Pin_0, C10.-, R12.Pin_0, R14.Pin_1, C12.-, C25.0
  N6: J28.pin2, C3.-, J51.pin2, J56.pin2, J60.pin2, R10.Pin_1, R15.Pin_1, C25.1, D1.cathode
  N7: J29.pin1, C2.+
  N8: J29.pin2, C1.-
  N9: J30.pin1, C3.+
  N10: J30.pin2, C1.+
  N11: Raspberry_Pi1.5V, J31.pin1, D1.anode
  N12: MIC1.pin2, R12.Pin_1, C11.0
  N13: MIC2.pin2, R8.Pin_0, C9.0
  N14: J48.pin1, R6.Pin_1, C7.1
  N15: J53.pin2, C8.1, R7.Pin_1
  N16: C5.0, R1.Pin_0
  N17: J55.pin1, R2.Pin_0, R6.Pin_0
  N18: J57.pin1, C11.1, R13.Pin_0
  N19: J58.pin2, R1.Pin_1, R2.Pin_1
  N20: J59.pin1, R4.Pin_0, R7.Pin_0
  N21: J61.pin1, C9.1, R9.Pin_1
  N22: J62.pin2, R3.Pin_1, R4.Pin_1
  N23: C6.0, R3.Pin_0
  N24: R9.Pin_0, R10.Pin_0, R11.Pin_1, C10.+
  N25: R13.Pin_1, R14.Pin_0, R15.Pin_0, C12.+
  N26: J66.pin1, J85.pin1
  N27: J67.pin1, R18.Pin_0, R20.Pin_0
  N28: J70.pin2, C15.-, J101.pin2, J102.pin2, R27.Pin_1, C26.0, U1.input_voltage, C27.+, C28.+
  N29: J76.pin1, C22.1, R25.Pin_0
  N30: J76.pin2, C14.+, J97.pin1, J101.pin1, J102.pin1, J104.pin1, MIC3.pin1, C18.1, J120.pin2, C19.0, R23.Pin_0, R28.Pin_1, C24.-, C26.1, VCC1.-, C27.-, C28.-, C29.1, C30.-
  N31: J78.pin2, R18.Pin_1, R19.Pin_1
  N32: C13.-, J90.pin2
  N33: C13.+, J82.pin2
  N34: C14.-, J106.pin1
  N35: C15.+, J82.pin1
  N36: C16.-, J106.pin2
  N37: C16.+, J90.pin1
  N38: J94.pin2, J104.pin2
  N39: J105.pin2, C19.1, R20.Pin_1
  N40: MIC3.pin2, R23.Pin_1, C22.0
  N41: C18.0, R19.Pin_0
  N42: J120.pin1, VCC1.+, D2.anode
  N43: R25.Pin_1, R27.Pin_0, R28.Pin_0, C24.+
  N44: U1.output_voltage, L1.pin_0, C29.0, C30.+
  N45: D2.cathode, L1.pin_1
